// Logisim project Projet_ARCHI.circ as structural Verilog: 9 circuits, main circuit main
module main (
);


  // Notes on the sheet:
  //   Solenn Beuvant
  //   585K
  //   Bastien Coutand
  //   Projet - Réalisation du SC-1
  //   Architecture des Ordinateurs - X31I050
  //   circuit visible dans la partie SC-1
  //   Université de Nantes
  //   2020/2021
endmodule

module SC_1 (
  output [7:0] Rs,
  output [7:0] Rt
);

  wire decodeur_instruction_1_isjump, decodeur_instruction_1_isload, decodeur_instruction_1_regwrite,
       horloge_out, reset;
  wire [1:0] controle_saut_1_nextpcselect;
  wire [2:0] decodeur_instruction_1_ctrlual;
  wire [3:0] selection_registres_1_rd, selection_registres_1_rs, selection_registres_1_rt_2,
       ual_8_bits_1_out_5;
  wire [7:0] adder_1_out, adder_2_out, bit_extender_1_out, multiplexer_1_out, multiplexer_2_out, PC_q,
       ual_8_bits_1_s;
  wire [15:0] ram_1_data;

  Button u_reset (.out(reset));
  Register PC (.D(multiplexer_2_out), .Q(PC_q), .clk(horloge_out), .clr(reset));  // open: en
  Clock horloge (.out(horloge_out));
  Adder adder_1 (.a(PC_q), .b(8'h1), .out(adder_1_out));  // open: cin, cout
  RAM #(.dataWidth(16)) ram_1 (.addr(PC_q), .data(ram_1_data), .clk(horloge_out), .ld(1'b1));  // open: sel, clr
  Decodeur_instruction decodeur_instruction_1 (
    .isJump(decodeur_instruction_1_isjump), .regWrite(decodeur_instruction_1_regwrite),
    .isLoad(decodeur_instruction_1_isload), .ctrlUAL(decodeur_instruction_1_ctrlual),
    .opcode(ram_1_data[15:12]));
  Multiplexer #(.width(8), .enable("false")) multiplexer_1 (
    .in0(ual_8_bits_1_s), .in1(ram_1_data[7:0]), .out(multiplexer_1_out), .sel(decodeur_instruction_1_isload));
  selection_registres selection_registres_1 (
    .rd_rs(ram_1_data[11:8]), .rs_rt(ram_1_data[7:4]), .rt(ram_1_data[3:0]),
    .isJMP(decodeur_instruction_1_isjump), .rs(selection_registres_1_rs), .rt_2(selection_registres_1_rt_2),
    .rd(selection_registres_1_rd));
  banc_de_registres banc_de_registres_1 (
    .rd(selection_registres_1_rd), .rs(selection_registres_1_rs), .rt(selection_registres_1_rt_2),
    .regWrite(decodeur_instruction_1_regwrite), .valIn(multiplexer_1_out), .Clock(horloge_out), .Rs_2(Rs),
    .Rt_2(Rt), .RESET(reset));
  assign bit_extender_1_out = {{4{ram_1_data[3]}}, ram_1_data[3:0]};  // Bit_Extender bit_extender_1
  Adder adder_2 (.a(adder_1_out), .b(bit_extender_1_out), .out(adder_2_out));  // open: cin, cout
  Multiplexer #(.select(2), .width(8), .enable("false")) multiplexer_2 (
    .in0(adder_1_out), .in1({8{1'b1}}), .in2(adder_2_out), .out(multiplexer_2_out),
    .sel(controle_saut_1_nextpcselect));  // open: in3
  UAL_8_bits ual_8_bits_1 (
    .A(Rs), .B(Rt), .CtrlUAL(decodeur_instruction_1_ctrlual), .S(ual_8_bits_1_s), .out_5(ual_8_bits_1_out_5));
  Controle_saut controle_saut_1 (
    .nextPCselect(controle_saut_1_nextpcselect), .opCode(ram_1_data[15:12]), .flag(ual_8_bits_1_out_5));

  // Notes on the sheet:
  //   <15:12>
  //   {op}
  //   isJMP
  //   regWrite
  //   valIn
  //   <11:8>
  //   {rd/rs}
  //   "HALT"
  //   <7:4>
  //   {rs/rt}
  //   isLoad
  //   "instruction suivante"
  //   <3:0>
  //   {rt}
  //   <7:0>
  //   {val}
  //   <3:0>
  //   {offset}
  //   Rs
  //   Rt
  //   "saut"
  //   CF, ZF, SF, OF
  //   ctrlUAL
  //   nextPCselect
endmodule

module Decodeur_instruction (
  input  [3:0] opcode,
  output isJump,
  output regWrite,
  output isLoad,
  output [2:0] ctrlUAL
);

  wire and_2_out, and_3_out, and_4_out, and_5_out, or_1_out;

  or or_1 (or_1_out, opcode[2], opcode[1], opcode[0]);
  not not_1 (regWrite, opcode[3]);
  and and_1 (isLoad, ~opcode[3], opcode[2], opcode[1], opcode[0]);  // AND_Gate
  and and_2 (and_2_out, ~opcode[3], opcode[1]);  // AND_Gate
  and and_3 (and_3_out, opcode[3], ~opcode[2], ~opcode[1], ~opcode[0]);  // AND_Gate
  and and_4 (and_4_out, ~opcode[3], opcode[2]);  // AND_Gate
  and and_5 (and_5_out, opcode[3], ~opcode[2], ~opcode[1], ~opcode[0]);  // AND_Gate
  or or_2 (ctrlUAL[0], opcode[3], opcode[0]);
  or or_3 (ctrlUAL[1], and_2_out, and_3_out);
  or or_4 (ctrlUAL[2], and_4_out, and_5_out);
  and and_6 (isJump, opcode[3], or_1_out);

  // Notes on the sheet:
  //   111 pour 1000 et 0111 car cela ne produit rien dans l'UAL
endmodule

module Controle_saut (
  input  [3:0] opCode,
  input  [3:0] flag,
  output [1:0] nextPCselect
);

  wire b_out, beq_out, bge_out, bgt_out, ble_out, blt_out, bne_out, or_1_out, or_2_out, xnor_1_out,
       xnor_2_out, xor_1_out, xor_2_out;

  xnor xnor_1 (xnor_1_out, flag[1], flag[0]);
  xor xor_1 (xor_1_out, flag[1], flag[0]);
  xnor xnor_2 (xnor_2_out, flag[1], flag[0]);
  xor xor_2 (xor_2_out, flag[1], flag[0]);
  or or_1 (or_1_out, flag[2], xnor_1_out);
  or or_2 (or_2_out, flag[2], xor_1_out);
  and halt (nextPCselect[0], opCode[3], ~opCode[2], ~opCode[1], ~opCode[0]);  // AND_Gate
  and b (b_out, opCode[3], ~opCode[2], ~opCode[1], opCode[0]);  // AND_Gate
  and beq (beq_out, opCode[3], ~opCode[2], opCode[1], ~opCode[0], flag[2]);  // AND_Gate
  and bne (bne_out, opCode[3], ~opCode[2], opCode[1], opCode[0], ~flag[2]);  // AND_Gate
  and bge (bge_out, opCode[3], opCode[2], ~opCode[1], ~opCode[0], or_1_out);  // AND_Gate
  and ble (ble_out, opCode[3], opCode[2], ~opCode[1], opCode[0], or_2_out);  // AND_Gate
  and bgt (bgt_out, opCode[3], opCode[2], opCode[1], ~opCode[0], ~flag[2], xnor_2_out);  // AND_Gate
  and blt (blt_out, opCode[3], opCode[2], opCode[1], opCode[0], ~flag[2], xor_2_out);  // AND_Gate
  or or_3 (nextPCselect[1], b_out, beq_out, bne_out, bge_out, ble_out, bgt_out, blt_out);

  // Notes on the sheet:
  //   Cf, Zf, Sf, Of
endmodule

module UAL_8_bits (
  input  [7:0] A,
  input  [7:0] B,
  input  [2:0] CtrlUAL,
  output [7:0] S,
  output [3:0] out_5
);

  wire Cf_Add, Cf_Sous, of_1_of_plus, of_2_of_minus;
  wire [7:0] adder_1_out, and_1_out, not_1_out, or_1_out, shifter_1_out, shifter_2_out, subtractor_1_out;

  Adder adder_1 (.a(A), .b(B), .out(adder_1_out), .cout(Cf_Add));  // open: cin
  Subtractor subtractor_1 (.a(A), .b(B), .out(subtractor_1_out), .bout(Cf_Sous));  // open: bin
  assign and_1_out = A & B;  // AND_Gate and_1, 8 bits wide
  assign or_1_out = A | B;  // OR_Gate or_1, 8 bits wide
  assign not_1_out = ~A;  // NOT_Gate not_1, 8 bits wide
  Shifter shifter_1 (.in(A), .\dist (B[2:0]), .out(shifter_1_out));
  Shifter #(.shift("lr")) shifter_2 (.in(A), .\dist (B[2:0]), .out(shifter_2_out));
  Multiplexer #(.select(3), .width(8), .enable("false")) multiplexer_1 (
    .in0(adder_1_out), .in1(subtractor_1_out), .in2(and_1_out), .in3(or_1_out), .in4(not_1_out),
    .in5(shifter_1_out), .in6(shifter_2_out), .in7({8{1'b0}}), .out({out_5[1], S[6:0]}), .sel(CtrlUAL));
  Of of_1 (.Of_plus(of_1_of_plus), .A(A), .B(B), .Sf(out_5[1]));
  Of_2 of_2 (.Of_minus(of_2_of_minus), .A(A), .B(B), .Sf(out_5[1]));
  Multiplexer #(.select(3), .enable("false")) multiplexer_2 (
    .in0(Cf_Add), .in1(Cf_Sous), .in2(1'b0), .in3(1'b0), .in4(1'b0), .in5(1'b0), .in6(1'b0), .in7(1'b0),
    .out(out_5[3]), .sel(CtrlUAL));
  Multiplexer #(.select(3), .enable("false")) multiplexer_3 (
    .in0(of_1_of_plus), .in1(of_2_of_minus), .in2(1'b0), .in3(1'b0), .in4(1'b0), .in5(1'b0), .in6(1'b0),
    .in7(1'b0), .out(out_5[0]), .sel(CtrlUAL));
  nor nor_1 (out_5[2], S[0], S[1], S[2], S[3], S[4], S[5], S[6], out_5[1]);

  assign S[7] = out_5[1];

  // Other names for the same wires on the sheet: Of = out_5[0]; Sf = out_5[1]; Zf = out_5[2]; Cf = out_5[3];
  //   Rs[7:0] = A; Rt[7:0] = B

  // Notes on the sheet:
  //   Rd <-- Rs << Rt
  //   3 premiers bits de Rt car Rs (8bits), donc 2³ == 8
  //   Overflow :
  //   * nombre binaire négatif = (-)
  //   * nombre binaire positif  = (+)
  //   --> ((+) + (+) = (-) ou (-) + (-) = (+))
  //   --> ((+) - (-) = (-)  ou (-) - (+) = (+))
endmodule

module Of (
  input  [7:0] A,
  input  [7:0] B,
  input  Sf,
  output Of_plus
);

  wire and_1_out, and_2_out;

  and and_1 (and_1_out, A[7], B[7], ~Sf);  // AND_Gate
  and and_2 (and_2_out, ~A[7], ~B[7], Sf);  // AND_Gate
  or or_1 (Of_plus, and_1_out, and_2_out);
endmodule

module Of_2 (
  input  [7:0] A,
  input  [7:0] B,
  input  Sf,
  output Of_minus
);

  wire and_1_out, and_2_out;

  and and_1 (and_1_out, A[7], ~B[7], ~Sf);  // AND_Gate
  and and_2 (and_2_out, ~A[7], B[7], Sf);  // AND_Gate
  or or_1 (Of_minus, and_1_out, and_2_out);
endmodule

module banc_de_registres (
  input  [3:0] rd,
  input  [3:0] rs,
  input  [3:0] rt,
  input  regWrite,
  input  [7:0] valIn,
  input  Clock,
  input  RESET,
  output [7:0] Rs_2,
  output [7:0] Rt_2
);

  wire and_1_out, and_2_out, and_3_out, and_4_out, and_5_out, and_6_out, and_7_out, and_8_out, and_9_out,
       and_10_out, and_11_out, and_12_out, and_13_out, and_14_out, and_15_out, and_16_out, decoder_1_out0,
       decoder_1_out1, decoder_1_out2, decoder_1_out3, decoder_1_out4, decoder_1_out5, decoder_1_out6,
       decoder_1_out7, decoder_1_out8, decoder_1_out9, decoder_1_out10, decoder_1_out11, decoder_1_out12,
       decoder_1_out13, decoder_1_out14, decoder_1_out15;
  wire [7:0] register_1_q, register_2_q, register_3_q, register_4_q, register_5_q, register_6_q,
       register_7_q, register_8_q, register_9_q, register_10_q, register_11_q, register_12_q, register_13_q,
       register_14_q, register_15_q, register_16_q;

  Decoder #(.select(4), .enable("false")) decoder_1 (
    .out0(decoder_1_out0), .out1(decoder_1_out1), .out2(decoder_1_out2), .out3(decoder_1_out3),
    .out4(decoder_1_out4), .out5(decoder_1_out5), .out6(decoder_1_out6), .out7(decoder_1_out7),
    .out8(decoder_1_out8), .out9(decoder_1_out9), .out10(decoder_1_out10), .out11(decoder_1_out11),
    .out12(decoder_1_out12), .out13(decoder_1_out13), .out14(decoder_1_out14), .out15(decoder_1_out15),
    .sel(rd));
  and and_1 (and_1_out, decoder_1_out0, regWrite);
  and and_2 (and_2_out, decoder_1_out1, regWrite);
  and and_3 (and_3_out, decoder_1_out2, regWrite);
  and and_4 (and_4_out, decoder_1_out3, regWrite);
  and and_5 (and_5_out, decoder_1_out4, regWrite);
  and and_6 (and_6_out, decoder_1_out5, regWrite);
  and and_7 (and_7_out, decoder_1_out6, regWrite);
  and and_8 (and_8_out, decoder_1_out7, regWrite);
  and and_9 (and_9_out, decoder_1_out8, regWrite);
  and and_10 (and_10_out, decoder_1_out9, regWrite);
  and and_11 (and_11_out, decoder_1_out10, regWrite);
  and and_12 (and_12_out, decoder_1_out11, regWrite);
  and and_13 (and_13_out, decoder_1_out12, regWrite);
  and and_14 (and_14_out, decoder_1_out13, regWrite);
  and and_15 (and_15_out, decoder_1_out14, regWrite);
  and and_16 (and_16_out, decoder_1_out15, regWrite);
  Register register_1 (.D(valIn), .en(and_1_out), .Q(register_1_q), .clk(Clock), .clr(RESET));
  Register register_2 (.D(valIn), .en(and_2_out), .Q(register_2_q), .clk(Clock), .clr(RESET));
  Register register_3 (.D(valIn), .en(and_3_out), .Q(register_3_q), .clk(Clock), .clr(RESET));
  Register register_4 (.D(valIn), .en(and_4_out), .Q(register_4_q), .clk(Clock), .clr(RESET));
  Register register_5 (.D(valIn), .en(and_5_out), .Q(register_5_q), .clk(Clock), .clr(RESET));
  Register register_6 (.D(valIn), .en(and_6_out), .Q(register_6_q), .clk(Clock), .clr(RESET));
  Register register_7 (.D(valIn), .en(and_7_out), .Q(register_7_q), .clk(Clock), .clr(RESET));
  Register register_8 (.D(valIn), .en(and_8_out), .Q(register_8_q), .clk(Clock), .clr(RESET));
  Register register_9 (.D(valIn), .en(and_9_out), .Q(register_9_q), .clk(Clock), .clr(RESET));
  Register register_10 (.D(valIn), .en(and_10_out), .Q(register_10_q), .clk(Clock), .clr(RESET));
  Register register_11 (.D(valIn), .en(and_11_out), .Q(register_11_q), .clk(Clock), .clr(RESET));
  Register register_12 (.D(valIn), .en(and_12_out), .Q(register_12_q), .clk(Clock), .clr(RESET));
  Register register_13 (.D(valIn), .en(and_13_out), .Q(register_13_q), .clk(Clock), .clr(RESET));
  Register register_14 (.D(valIn), .en(and_14_out), .Q(register_14_q), .clk(Clock), .clr(RESET));
  Register register_15 (.D(valIn), .en(and_15_out), .Q(register_15_q), .clk(Clock), .clr(RESET));
  Register register_16 (.D(valIn), .en(and_16_out), .Q(register_16_q), .clk(Clock), .clr(RESET));
  Multiplexer #(.select(4), .width(8), .enable("false")) multiplexer_1 (
    .in0(register_1_q), .in1(register_2_q), .in2(register_3_q), .in3(register_4_q), .in4(register_5_q),
    .in5(register_6_q), .in6(register_7_q), .in7(register_8_q), .in8(register_9_q), .in9(register_10_q),
    .in10(register_11_q), .in11(register_12_q), .in12(register_13_q), .in13(register_14_q),
    .in14(register_15_q), .in15(register_16_q), .out(Rs_2), .sel(rs));
  Multiplexer #(.select(4), .width(8), .enable("false")) multiplexer_2 (
    .in0(register_1_q), .in1(register_2_q), .in2(register_3_q), .in3(register_4_q), .in4(register_5_q),
    .in5(register_6_q), .in6(register_7_q), .in7(register_8_q), .in8(register_9_q), .in9(register_10_q),
    .in10(register_11_q), .in11(register_12_q), .in12(register_13_q), .in13(register_14_q),
    .in14(register_15_q), .in15(register_16_q), .out(Rt_2), .sel(rt));
endmodule

module selection_registres (
  input  [3:0] rd_rs,
  input  [3:0] rs_rt,
  input  [3:0] rt,
  input  isJMP,
  output [3:0] rd,
  output [3:0] rs,
  output [3:0] rt_2
);

  Multiplexer #(.width(4), .enable("false")) multiplexer_1 (.in0(rd_rs), .in1(4'b0000), .out(rd), .sel(isJMP));
  Multiplexer #(.width(4), .enable("false")) multiplexer_2 (.in0(rs_rt), .in1(rd_rs), .out(rs), .sel(isJMP));
  Multiplexer #(.width(4), .enable("false")) multiplexer_3 (.in0(rt), .in1(rs_rt), .out(rt_2), .sel(isJMP));
endmodule
